// Logisim project tp.circ as structural Verilog: 9 circuits, main circuit principal
module main (
);

  wire clock_1_out, clock_2_out, clock_3_out, clock_4_out, decoder_1_out0, decoder_1_out1, decoder_1_out2,
       decoder_1_out3, decoder_1_out4, decoder_1_out5, decoder_1_out6, decoder_1_out7, decoder_1_out8,
       decoder_1_out9, decoder_1_out10, decoder_1_out11, decoder_1_out12, decoder_1_out13, decoder_1_out14,
       decoder_1_out15, j_k_ff_1_qn, j_k_ff_2_qn, j_k_ff_3_qn, j_k_ff_4_qn, j_k_ff_5_qn, j_k_ff_6_qn,
       j_k_ff_7_qn, j_k_ff_8_qn, j_k_ff_9_qn, j_k_ff_10_qn, j_k_ff_11_qn, j_k_ff_12_qn, or_1_out;
  wire [3:0] j_k_ff_1_q;

  Clock clock_1 (.out(clock_1_out));
  Clock clock_2 (.out(clock_2_out));
  Clock clock_3 (.out(clock_3_out));
  Clock clock_4 (.out(clock_4_out));
  J_K_Flip_Flop j_k_ff_1 (
    .J(1'b1), .clk(clock_1_out), .K(1'b1), .Q(j_k_ff_1_q[0]), .Qn(j_k_ff_1_qn));  // open: preset, en, reset
  J_K_Flip_Flop j_k_ff_2 (.J(1'b1), .clk(clock_2_out), .K(1'b1), .Qn(j_k_ff_2_qn));  // open: Q, preset, en, reset
  J_K_Flip_Flop j_k_ff_3 (.J(1'b1), .clk(clock_3_out), .K(1'b1), .Qn(j_k_ff_3_qn));  // open: Q, preset, en, reset
  J_K_Flip_Flop j_k_ff_4 (.J(1'b1), .clk(clock_4_out), .K(1'b1), .Qn(j_k_ff_4_qn));  // open: Q, preset, en, reset
  J_K_Flip_Flop j_k_ff_5 (
    .J(1'b1), .clk(j_k_ff_1_qn), .K(1'b1), .Q(j_k_ff_1_q[1]), .Qn(j_k_ff_5_qn));  // open: preset, en, reset
  J_K_Flip_Flop j_k_ff_6 (.J(1'b1), .clk(j_k_ff_2_qn), .K(1'b1), .Qn(j_k_ff_6_qn));  // open: Q, preset, en, reset
  J_K_Flip_Flop j_k_ff_7 (.J(1'b1), .clk(j_k_ff_3_qn), .K(1'b1), .Qn(j_k_ff_7_qn));  // open: Q, preset, en, reset
  J_K_Flip_Flop j_k_ff_8 (.J(1'b1), .clk(j_k_ff_4_qn), .K(1'b1), .Qn(j_k_ff_8_qn));  // open: Q, preset, en, reset
  J_K_Flip_Flop j_k_ff_9 (
    .J(1'b1), .clk(j_k_ff_5_qn), .K(1'b1), .Q(j_k_ff_1_q[2]), .Qn(j_k_ff_9_qn));  // open: preset, en, reset
  J_K_Flip_Flop j_k_ff_10 (.J(1'b1), .clk(j_k_ff_6_qn), .K(1'b1), .Qn(j_k_ff_10_qn));  // open: Q, preset, en, reset
  J_K_Flip_Flop j_k_ff_11 (.J(1'b1), .clk(j_k_ff_7_qn), .K(1'b1), .Qn(j_k_ff_11_qn));  // open: Q, preset, en, reset
  J_K_Flip_Flop j_k_ff_12 (.J(1'b1), .clk(j_k_ff_8_qn), .K(1'b1), .Qn(j_k_ff_12_qn));  // open: Q, preset, en, reset
  J_K_Flip_Flop j_k_ff_13 (.J(1'b1), .clk(j_k_ff_9_qn), .K(1'b1), .Q(j_k_ff_1_q[3]));  // open: Qn, preset, en, reset
  J_K_Flip_Flop j_k_ff_14 (.J(1'b1), .clk(j_k_ff_10_qn), .K(1'b1));  // open: Q, Qn, preset, en, reset
  J_K_Flip_Flop j_k_ff_15 (.J(1'b1), .clk(j_k_ff_11_qn), .K(1'b1));  // open: Q, Qn, preset, en, reset
  J_K_Flip_Flop j_k_ff_16 (.J(1'b1), .clk(j_k_ff_12_qn), .K(1'b1));  // open: Q, Qn, preset, en, reset
  Decoder #(.select(4), .enable("false")) decoder_1 (
    .out0(decoder_1_out0), .out1(decoder_1_out1), .out2(decoder_1_out2), .out3(decoder_1_out3),
    .out4(decoder_1_out4), .out5(decoder_1_out5), .out6(decoder_1_out6), .out7(decoder_1_out7),
    .out8(decoder_1_out8), .out9(decoder_1_out9), .out10(decoder_1_out10), .out11(decoder_1_out11),
    .out12(decoder_1_out12), .out13(decoder_1_out13), .out14(decoder_1_out14), .out15(decoder_1_out15),
    .sel(j_k_ff_1_q));
  or or_1 (or_1_out, decoder_1_out2, decoder_1_out3, decoder_1_out4, decoder_1_out5, decoder_1_out6, decoder_1_out8, decoder_1_out9);
  _7_Segment_Display u_7_segment_display_1 (.g(or_1_out));  // open: f, a, b, e, d, c, dp
  _7_Segment_Display u_7_segment_display_2 (.g(1'b1));  // open: f, a, b, e, d, c, dp
endmodule

// CONTADOR
module contador (
  input  \BOTÃO ,
  input  CLEAR,
  input  ENABLE,
  output [8:0] out_4
);

  wire j_k_ff_1_qn, j_k_ff_2_qn, j_k_ff_3_qn, j_k_ff_4_qn, j_k_ff_5_qn, j_k_ff_6_qn, j_k_ff_7_qn, j_k_ff_8_qn;

  J_K_Flip_Flop j_k_ff_1 (
    .J(1'b1), .clk(\BOTÃO ), .K(1'b1), .Q(out_4[0]), .Qn(j_k_ff_1_qn), .en(ENABLE), .reset(CLEAR));  // open: preset
  J_K_Flip_Flop j_k_ff_2 (
    .J(1'b1), .clk(j_k_ff_1_qn), .K(1'b1), .Q(out_4[1]), .Qn(j_k_ff_2_qn), .en(ENABLE), .reset(CLEAR));  // open: preset
  J_K_Flip_Flop j_k_ff_3 (
    .J(1'b1), .clk(j_k_ff_2_qn), .K(1'b1), .Q(out_4[2]), .Qn(j_k_ff_3_qn), .en(ENABLE), .reset(CLEAR));  // open: preset
  J_K_Flip_Flop j_k_ff_4 (
    .J(1'b1), .clk(j_k_ff_3_qn), .K(1'b1), .Q(out_4[3]), .Qn(j_k_ff_4_qn), .en(ENABLE), .reset(CLEAR));  // open: preset
  J_K_Flip_Flop j_k_ff_5 (
    .J(1'b1), .clk(j_k_ff_4_qn), .K(1'b1), .Q(out_4[4]), .Qn(j_k_ff_5_qn), .en(ENABLE), .reset(CLEAR));  // open: preset
  J_K_Flip_Flop j_k_ff_6 (
    .J(1'b1), .clk(j_k_ff_5_qn), .K(1'b1), .Q(out_4[5]), .Qn(j_k_ff_6_qn), .en(ENABLE), .reset(CLEAR));  // open: preset
  J_K_Flip_Flop j_k_ff_7 (
    .J(1'b1), .clk(j_k_ff_6_qn), .K(1'b1), .Q(out_4[6]), .Qn(j_k_ff_7_qn), .en(ENABLE), .reset(CLEAR));  // open: preset
  J_K_Flip_Flop j_k_ff_8 (
    .J(1'b1), .clk(j_k_ff_7_qn), .K(1'b1), .Q(out_4[7]), .Qn(j_k_ff_8_qn), .en(ENABLE), .reset(CLEAR));  // open: preset
  J_K_Flip_Flop j_k_ff_9 (
    .J(1'b1), .clk(j_k_ff_8_qn), .K(1'b1), .Q(out_4[8]), .en(ENABLE), .reset(CLEAR));  // open: Qn, preset
endmodule

module principal (
  input  ENABLE,
  input  EDISPLAY
);

  wire BOM_out, OTIMO_out, PESSIMO_out, REGULAR_out, RESETA_CONTAGEM_out, RUIM_out;
  wire [3:0] separador_decod_1_out_3, separador_decod_1_out_4, separador_decod_1_out_5,
       separador_decod_2_out_3, separador_decod_2_out_4, separador_decod_2_out_5, separador_decod_3_out_3,
       separador_decod_3_out_4, separador_decod_3_out_5, separador_decod_4_out_3, separador_decod_4_out_4,
       separador_decod_4_out_5, separador_decod_5_out_3, separador_decod_5_out_4, separador_decod_5_out_5;
  wire [8:0] contador_1_out_4, contador_2_out_4, contador_3_out_4, contador_4_out_4, contador_5_out_4;

  contador contador_1 (.\BOTÃO (OTIMO_out), .CLEAR(RESETA_CONTAGEM_out), .ENABLE(ENABLE), .out_4(contador_1_out_4));
  Button OTIMO (.out(OTIMO_out));
  contador contador_2 (.\BOTÃO (BOM_out), .CLEAR(RESETA_CONTAGEM_out), .ENABLE(ENABLE), .out_4(contador_2_out_4));
  Button BOM (.out(BOM_out));
  contador contador_3 (.\BOTÃO (REGULAR_out), .CLEAR(RESETA_CONTAGEM_out), .ENABLE(ENABLE), .out_4(contador_3_out_4));
  Button REGULAR (.out(REGULAR_out));
  contador contador_4 (.\BOTÃO (RUIM_out), .CLEAR(RESETA_CONTAGEM_out), .ENABLE(ENABLE), .out_4(contador_4_out_4));
  Button RUIM (.out(RUIM_out));
  contador contador_5 (.\BOTÃO (PESSIMO_out), .CLEAR(RESETA_CONTAGEM_out), .ENABLE(ENABLE), .out_4(contador_5_out_4));
  Button PESSIMO (.out(PESSIMO_out));
  Button RESETA_CONTAGEM (.out(RESETA_CONTAGEM_out));
  separador_decod separador_decod_1 (
    .in_1(contador_1_out_4), .ENABLE(EDISPLAY), .out_3(separador_decod_1_out_3),
    .out_4(separador_decod_1_out_4), .out_5(separador_decod_1_out_5));
  separador_decod separador_decod_2 (
    .in_1(contador_2_out_4), .ENABLE(EDISPLAY), .out_3(separador_decod_2_out_3),
    .out_4(separador_decod_2_out_4), .out_5(separador_decod_2_out_5));
  separador_decod separador_decod_3 (
    .in_1(contador_3_out_4), .ENABLE(EDISPLAY), .out_3(separador_decod_3_out_3),
    .out_4(separador_decod_3_out_4), .out_5(separador_decod_3_out_5));
  separador_decod separador_decod_4 (
    .in_1(contador_4_out_4), .ENABLE(EDISPLAY), .out_3(separador_decod_4_out_3),
    .out_4(separador_decod_4_out_4), .out_5(separador_decod_4_out_5));
  separador_decod separador_decod_5 (
    .in_1(contador_5_out_4), .ENABLE(EDISPLAY), .out_3(separador_decod_5_out_3),
    .out_4(separador_decod_5_out_4), .out_5(separador_decod_5_out_5));
  Hex_Digit_Display hex_digit_display_1 (.value(separador_decod_1_out_4));  // open: dp
  Hex_Digit_Display hex_digit_display_2 (.value(separador_decod_1_out_3));  // open: dp
  Hex_Digit_Display hex_digit_display_3 (.value(separador_decod_2_out_3));  // open: dp
  Hex_Digit_Display hex_digit_display_4 (.value(separador_decod_2_out_4));  // open: dp
  Hex_Digit_Display hex_digit_display_5 (.value(separador_decod_3_out_4));  // open: dp
  Hex_Digit_Display hex_digit_display_6 (.value(separador_decod_3_out_3));  // open: dp
  Hex_Digit_Display hex_digit_display_7 (.value(separador_decod_4_out_4));  // open: dp
  Hex_Digit_Display hex_digit_display_8 (.value(separador_decod_4_out_3));  // open: dp
  Hex_Digit_Display hex_digit_display_9 (.value(separador_decod_5_out_3));  // open: dp
  Hex_Digit_Display hex_digit_display_10 (.value(separador_decod_5_out_4));  // open: dp
  Hex_Digit_Display hex_digit_display_11 (.value(separador_decod_1_out_5));  // open: dp
  Hex_Digit_Display hex_digit_display_12 (.value(separador_decod_2_out_5));  // open: dp
  Hex_Digit_Display hex_digit_display_13 (.value(separador_decod_3_out_5));  // open: dp
  Hex_Digit_Display hex_digit_display_14 (.value(separador_decod_4_out_5));  // open: dp
  Hex_Digit_Display hex_digit_display_15 (.value(separador_decod_5_out_5));  // open: dp
  DotMatrix dotmatrix_1 ();  // open: col0, col1, col2, col3, col4
endmodule

module maior_que_9 (
  input  A0,
  input  A1,
  input  A2,
  input  A3,
  input  A4,
  output \VERIFICAÇÃO 
);

  wire and_1_out, or_1_out;

  or or_1 (or_1_out, A1, A2);
  and and_1 (and_1_out, or_1_out, A3);
  or or_2 (\VERIFICAÇÃO , and_1_out, A4);
endmodule

module decodificador (
  input  [3:0] in_1,
  output out_2,
  output out_3,
  output out_4,
  output out_5,
  output out_6,
  output out_7,
  output out_8,
  output out_9
);

  wire _0, _1, _2, _3, _4, _5, _6, _7, _8, _9;

  Decoder #(.select(4), .disabled(0), .enable("false")) decoder_1 (
    .out0(_0), .out1(_1), .out2(_2), .out3(_3), .out4(_4), .out5(_5), .out6(_6), .out7(_7), .out8(_8),
    .out9(_9), .sel(in_1));  // open: out10, out11, out12, out13, out14, out15
  or or_1 (out_2, _2, _3, _4, _5, _6, _8, _9);
  or or_2 (out_3, _0, _4, _5, _6, _8, _9);
  or or_3 (out_4, _0, _2, _3, _5, _6, _7, _8, _9);
  or or_4 (out_5, _0, _1, _2, _3, _4, _7, _8, _9);
  or or_5 (out_6, _0, _2, _6, _8);
  or or_6 (out_7, _0, _2, _3, _5, _6, _8, _9);
  or or_7 (out_8, _0, _1, _3, _4, _5, _6, _7, _8, _9);

  assign out_9 = 1'b0;
endmodule

module separadordecimal (
  input  in_1,
  input  in_2,
  input  in_3,
  input  in_4,
  input  in_5,
  input  in_6,
  input  in_7,
  input  in_8,
  input  in_9,
  output out_10,
  output out_11,
  output out_12,
  output out_13,
  output out_14,
  output out_15,
  output out_16,
  output out_17,
  output out_18,
  output out_19,
  output out_20,
  output out_21
);

  wire [8:0] divider_1_rem;
  wire [8:4] divider_1_out, divider_2_out, divider_2_rem;

  Divider #(.width(9)) divider_1 (
    .a({in_9, in_8, in_7, in_6, in_5, in_4, in_3, in_2, in_1}), .b(9'h64),
    .out({divider_1_out, out_10, out_11, out_12, out_13}), .rem(divider_1_rem));  // open: upper
  Divider #(.width(9)) divider_2 (
    .a(divider_1_rem), .b(9'ha), .out({divider_2_out, out_17, out_16, out_15, out_14}),
    .rem({divider_2_rem, out_18, out_19, out_20, out_21}));  // open: upper
endmodule

module separador_decod (
  input  [8:0] in_1,
  input  ENABLE,
  output [3:0] out_3,
  output [3:0] out_4,
  output [3:0] out_5
);

  wire [8:0] zeradistri_1_out_3;

  zeradistri zeradistri_1 (.in_1(in_1), .ENABLE(ENABLE), .out_3(zeradistri_1_out_3));
  separadordecimal separadordecimal_1 (
    .in_1(zeradistri_1_out_3[0]), .in_2(zeradistri_1_out_3[1]), .in_3(zeradistri_1_out_3[2]),
    .in_4(zeradistri_1_out_3[3]), .in_5(zeradistri_1_out_3[4]), .in_6(zeradistri_1_out_3[5]),
    .in_7(zeradistri_1_out_3[6]), .in_8(zeradistri_1_out_3[7]), .in_9(zeradistri_1_out_3[8]),
    .out_10(out_3[3]), .out_11(out_3[2]), .out_12(out_3[1]), .out_13(out_3[0]), .out_18(out_5[3]),
    .out_19(out_5[2]), .out_20(out_5[1]), .out_21(out_5[0]), .out_14(out_4[0]), .out_15(out_4[1]),
    .out_16(out_4[2]), .out_17(out_4[3]));
endmodule

module zeradistri (
  input  [8:0] in_1,
  input  ENABLE,
  output [8:0] out_3
);

  and and_1 (out_3[0], in_1[0], ENABLE);
  and and_2 (out_3[1], in_1[1], ENABLE);
  and and_3 (out_3[2], in_1[2], ENABLE);
  and and_4 (out_3[3], in_1[3], ENABLE);
  and and_5 (out_3[4], in_1[4], ENABLE);
  and and_6 (out_3[5], in_1[5], ENABLE);
  and and_7 (out_3[6], in_1[6], ENABLE);
  and and_8 (out_3[7], in_1[7], ENABLE);
  and and_9 (out_3[8], in_1[8], ENABLE);
endmodule

module codcaras (
  input  [2:0] in_1
);
endmodule
